# Fritzing sketch button_pi (saved by Fritzing 0.9.4)
breadboards: 1

parts:
  BTN(channel10) = Pushbutton [package="[SMD]"]
  BTN(channel18) = Pushbutton [package="[SMD]"]
  Raspberry_Pi = Raspberry Pi 3 [part_number=RPI-3-V1.2]
  Resistors = Resistor [tolerance=±5% resistance=10k package="0805 [SMD]"]
  R3 = Resistor [tolerance=±5% resistance=10k package="0805 [SMD]"]

nets:
  N1: BTN(channel10).Pin_1, BTN(channel10).Pin_2, BTN(channel18).Pin_3, BTN(channel18).Pin_4, Raspberry_Pi.3v3, R3.Pin_0
  N2: BTN(channel10).Pin_3, BTN(channel10).Pin_4, Resistors.Pin_1
  N3: BTN(channel18).Pin_1, BTN(channel18).Pin_2
  N4: Raspberry_Pi.GPIO24, R3.Pin_1
  N5: Raspberry_Pi.GPIO15, Resistors.Pin_0
